# Fritzing sketch Bus (saved by Fritzing 0.9.3b)

parts:
  Part1 = Arduino Uno (Rev3) - ICSP [part_number=uno]
  Part2 = RFID-RC522-v3
  WeMos_D1_Mini1 = WeMos D1 Mini [part_number=wifi]

nets:
  N1: Part1.D9_PWM, Part2.RST
  N2: Part1.D10_PWM/SS, Part2.SDA
  N3: Part1.D11_PWM/MOSI, Part2.MOSI
  N4: Part1.D12/MISO, Part2.MISO
  N5: Part1.D13/SCK, Part2.SCK
  N6: Part1.D0/RX, WeMos_D1_Mini1.TX
  N7: Part1.D1/TX, WeMos_D1_Mini1.RX
  3V3: Part1.3V3, Part2.3.3V
  5V: Part1.5V, WeMos_D1_Mini1.5V
  GND: Part1.GND, Part2.GND, WeMos_D1_Mini1.G

custom parts:
  RFID-RC522-v3: A simple China made RFID-RC522 Reader (6x4 cm); do check the pin labels, as this is a MFRC522 based clone.
